# Fritzing sketch airQualitySensor (saved by Fritzing 0.9.3b)
breadboards: 1

parts:
  U1 = NodeMCU V3.0
  U2 = Hirose DF13 Series Header [part_number=DF13#-8P-1.25V package=DF13C-8P-1.25V]

nets:
  N1: U1.GND#6, U1.GND#13, U1.GND#16, U1.GND#33, U2.2
  N2: U1.D7, U2.5
  N3: U1.D8, U2.4
  N4: U1.Vin, U2.1

custom parts:
  NodeMCU V3.0: ESP8266 based NodeMCU
